# Fritzing sketch tellus-rover-v2-design01a (saved by Fritzing 0.9.3b)
stripboards: 3

parts:
  M2 = DC Motor
  M4 = DC Motor
  IC5 = L293D [package=THT]
  Raspberry_Pi_Zero1 = Raspberry Pi Zero
  VCC1 = Battery

nets:
  N1: M2.pin_1, IC5.Out_2_(_Controlled_by_Enable_1_)
  N2: M2.pin_2, IC5.Out_1_(_Controlled_by_Enable_1_)
  N3: M4.pin_1, IC5.Out_4_(_Controlled_by_Enable_2_)
  N4: M4.pin_2, IC5.Out_3_(_Controlled_by_Enable_2_)
  N5: IC5.Enable_1, Raspberry_Pi_Zero1.GPIO19, Raspberry_Pi_Zero1.GPIO16
  N6: IC5.In_1, Raspberry_Pi_Zero1.GPIO12
  N7: IC5.0V, IC5.In_2, Raspberry_Pi_Zero1.GND, VCC1.-
  N8: IC5.+Vmotor, VCC1.+
  N9: IC5.Enable_2, Raspberry_Pi_Zero1.GPIO22
  N10: IC5.In_3, Raspberry_Pi_Zero1.GPIO10
  N11: IC5.In_4, Raspberry_Pi_Zero1.GPIO9
  3V3: Raspberry_Pi_Zero1.3v3, Raspberry_Pi_Zero1.3V3, Raspberry_Pi_Zero1.5V
